// Logisim project equality_detector.circ as structural Verilog: 1 circuit, main circuit 4 bit equality detector
module _4_bit_equality_detector (
  input  A0,
  input  B0,
  input  A1,
  input  B1,
  input  A2,
  input  B2,
  input  A3,
  input  B3,
  output out_9
);

  wire xnor_1_out, xnor_2_out, xnor_3_out, xnor_4_out;

  xnor xnor_1 (xnor_1_out, A0, B0);
  xnor xnor_2 (xnor_2_out, A1, B1);
  xnor xnor_3 (xnor_3_out, A2, B2);
  xnor xnor_4 (xnor_4_out, A3, B3);
  and and_1 (out_9, xnor_1_out, xnor_2_out, xnor_3_out, xnor_4_out);
endmodule
